# Fritzing sketch NMEALogger (saved by Fritzing 0.6.3b)

parts:
  Arduino2 = Arduino
  Part2 = MicroSD_Breakout_0544
  Part1 = GPS_LS20031
  LED1 = LED - 5mm [color="Red (633nm)" package="5 mm [THT]"]
  LED2 = LED - 5mm [color="Green (555nm)" package="5 mm [THT]"]

nets:
  N1: Arduino2.GND, Part2.connector2, Part1.connector10, LED2.cathode
  N2: Arduino2.D13, Part2.connector3
  N3: Arduino2.D12, Part2.connector1
  N4: Arduino2.D11, Part2.connector5
  N5: Arduino2.D10, Part2.connector6
  N6: Arduino2.D5, LED2.anode
  N7: Arduino2.D4, LED1.anode
  N8: Arduino2.D0RX, Part1.connector9
  N9: Arduino2.3V3, Part2.connector4, Part1.connector7
