# Fritzing sketch TemperatureLogger (saved by Fritzing 0.6.3b)

parts:
  Arduino1 = Arduino
  Part1 = MicroSD_Breakout_0544
  Thermistor-LM1 = LM35_Temperature_Sensor

nets:
  N1: Arduino1.GND, Part1.connector2, Thermistor-LM1.connector2
  N2: Arduino1.D13, Part1.connector3
  N3: Arduino1.D12, Part1.connector1
  N4: Arduino1.D11, Part1.connector5
  N5: Arduino1.D10, Part1.connector6
  N6: Arduino1.3V3, Part1.connector4
  N7: Arduino1.+5V, Thermistor-LM1.connector0
  N8: Arduino1.A0, Thermistor-LM1.connector1
